// Logisim project projekt_oiak(1).circ as structural Verilog: 9 circuits, main circuit full_adder
module full_adder (
  input  CIN,
  input  A,
  input  B
);

  wire and_1_out, and_2_out, or_1_out, xor_1_out, xor_2_out;

  xor xor_1 (xor_1_out, A, B);
  and and_1 (and_1_out, A, B);
  and and_2 (and_2_out, xor_1_out, CIN);
  xor xor_2 (xor_2_out, xor_1_out, CIN);
  or or_1 (or_1_out, and_2_out, and_1_out);

  // Notes on the sheet:
  //   S1
  //   C1
  //   S
  //   Cout
endmodule

module kompresor_4_2 (
  input  x1,
  input  x2,
  input  x3,
  input  x4,
  input  Cin
);

  wire and_1_out, and_2_out, and_3_out, and_4_out, xor_1_out, xor_2_out, xor_3_out;

  xor xor_1 (xor_1_out, x1, x2);
  and and_1 (and_1_out, x2, x1);
  xor xor_2 (xor_2_out, xor_1_out, x3);
  and and_2 (and_2_out, x3, xor_1_out);
  xor xor_3 (xor_3_out, xor_2_out, x4);
  and and_3 (and_3_out, x4, xor_2_out);
  // XOR_Gate xor_4 has open pins: in0=xor_3_out, in1=Cin, out=open
  and and_4 (and_4_out, Cin, xor_3_out);
  // OR_Gate or_1 has open pins: in0=and_2_out, in1=and_3_out, in2=and_4_out, out=open
  // OR_Gate or_2 has open pins: in0=and_2_out, in1=and_1_out, out=open

  // Notes on the sheet:
  //   t1
  //   t2
  //   t3
  //   t4
  //   t6
  //   t5
  //   Sum
  //   c_int
  //   Carry
  //   Cout
endmodule

module stala_ct (
  output out_1,
  output out_2,
  output out_3,
  output out_4,
  output out_5,
  output out_6,
  output out_7,
  output out_8
);


  assign out_1 = 1'b0;
  assign out_2 = 1'b1;
  assign out_3 = 1'b1;
  assign out_4 = 1'b0;
  assign out_5 = 1'b0;
  assign out_6 = 1'b0;
  assign out_7 = 1'b0;
  assign out_8 = 1'b0;
endmodule

module modul_korekcji_ecm (
);

  wire or_1_out, or_2_out;

  // OR_Gate or_1 has open pins: out=or_1_out
  // OR_Gate or_2 has open pins: out=or_2_out

  // Notes on the sheet:
  //   Carry_8
  //   Carry_9
endmodule

module Iloczyny_czesciowe (
  input  a0,
  input  a1,
  input  a2,
  input  a3,
  input  a4,
  input  a5,
  input  a6,
  input  b7,
  input  b0,
  input  b1,
  input  b2,
  input  b3,
  input  b4,
  input  b5,
  input  b6,
  input  b7_2
);

  wire and_1_out, and_2_out, and_3_out, and_4_out, and_5_out, and_6_out, and_7_out, and_8_out, and_9_out,
       and_10_out, and_11_out, and_12_out, and_13_out, and_14_out, and_15_out, and_16_out, and_17_out,
       and_18_out, and_19_out, and_20_out, and_21_out, and_22_out, and_23_out, and_24_out, and_25_out,
       and_26_out, and_27_out, and_28_out, and_29_out, and_30_out, and_31_out, and_32_out, and_33_out,
       and_34_out, and_35_out, and_36_out, and_37_out, and_38_out, and_39_out, and_40_out, and_41_out,
       and_42_out, and_43_out, and_44_out, and_45_out, and_46_out, and_47_out, and_48_out, and_49_out,
       and_50_out, and_51_out, and_52_out, and_53_out, and_54_out, and_55_out, and_56_out, and_57_out,
       and_58_out, and_59_out, and_60_out, and_61_out, and_62_out, and_63_out, and_64_out;

  and and_1 (and_1_out, b0, a0);
  and and_2 (and_2_out, b0, a0);
  and and_3 (and_3_out, b0, a0);
  and and_4 (and_4_out, b0, a0);
  and and_5 (and_5_out, b0, a0);
  and and_6 (and_6_out, b0, a0);
  and and_7 (and_7_out, b0, a0);
  and and_8 (and_8_out, b7_2, a0);
  and and_9 (and_9_out, b0, a1);
  and and_10 (and_10_out, b0, a1);
  and and_11 (and_11_out, b0, a1);
  and and_12 (and_12_out, b0, a1);
  and and_13 (and_13_out, b0, a1);
  and and_14 (and_14_out, b0, a1);
  and and_15 (and_15_out, b0, a1);
  and and_16 (and_16_out, b7_2, a1);
  and and_17 (and_17_out, b0, a2);
  and and_18 (and_18_out, b0, a2);
  and and_19 (and_19_out, b0, a2);
  and and_20 (and_20_out, b0, a2);
  and and_21 (and_21_out, b0, a2);
  and and_22 (and_22_out, b0, a2);
  and and_23 (and_23_out, b0, a2);
  and and_24 (and_24_out, b7_2, a2);
  and and_25 (and_25_out, b0, a3);
  and and_26 (and_26_out, b0, a3);
  and and_27 (and_27_out, b0, a3);
  and and_28 (and_28_out, b0, a3);
  and and_29 (and_29_out, b0, a3);
  and and_30 (and_30_out, b0, a3);
  and and_31 (and_31_out, b0, a3);
  and and_32 (and_32_out, b7_2, a3);
  and and_33 (and_33_out, b0, a4);
  and and_34 (and_34_out, b0, a4);
  and and_35 (and_35_out, b0, a4);
  and and_36 (and_36_out, b0, a4);
  and and_37 (and_37_out, b0, a4);
  and and_38 (and_38_out, b0, a4);
  and and_39 (and_39_out, b0, a4);
  and and_40 (and_40_out, b7_2, a4);
  and and_41 (and_41_out, b0, a5);
  and and_42 (and_42_out, b0, a5);
  and and_43 (and_43_out, b0, a5);
  and and_44 (and_44_out, b0, a5);
  and and_45 (and_45_out, b0, a5);
  and and_46 (and_46_out, b0, a5);
  and and_47 (and_47_out, b0, a5);
  and and_48 (and_48_out, b7_2, a5);
  and and_49 (and_49_out, b0, a6);
  and and_50 (and_50_out, b0, a6);
  and and_51 (and_51_out, b0, a6);
  and and_52 (and_52_out, b0, a6);
  and and_53 (and_53_out, b0, a6);
  and and_54 (and_54_out, b0, a6);
  and and_55 (and_55_out, b0, a6);
  and and_56 (and_56_out, b7_2, a6);
  and and_57 (and_57_out, b0, b0);
  and and_58 (and_58_out, b0, b0);
  and and_59 (and_59_out, b0, b0);
  and and_60 (and_60_out, b0, b0);
  and and_61 (and_61_out, b0, b0);
  and and_62 (and_62_out, b0, b0);
  and and_63 (and_63_out, b0, b0);
  and and_64 (and_64_out, b7_2, b0);

  assign b1 = b0;
  assign b2 = b0;
  assign b3 = b0;
  assign b4 = b0;
  assign b5 = b0;
  assign b6 = b0;
  assign b7 = b0;

  // Notes on the sheet:
  //   a0
  //   a1
  //   a2
  //   a3
  //   a4
  //   a5
  //   a6
  //   a7
  //   0
  //   1
  //   2
  //   3
  //   4
  //   5
  //   6
  //   7
  //   8
  //   9
  //   10
  //   11
  //   12
  //   13
  //   14
  //   kolumny 0 - 7 do wyjebania
  //   i zasąpić stałą
endmodule

module uklad_koncowy (
  input  a0,
  input  a1,
  input  a2,
  input  a3,
  input  a4,
  input  a5,
  input  a6,
  input  b7,
  input  b0,
  input  b1,
  input  b2,
  input  b3,
  input  b4,
  input  b5,
  input  b6,
  input  b7_2,
  input  Cin,
  input  cin_2,
  input  x4,
  input  Cin_3,
  input  x4_2,
  input  Cin_4
);

  wire and_1_out, and_2_out, and_3_out, and_4_out, and_5_out, and_6_out, and_7_out, and_8_out, and_9_out,
       and_10_out, and_11_out, and_12_out, and_13_out, and_14_out, and_15_out, and_16_out, and_17_out,
       and_18_out, and_19_out, and_20_out, and_21_out, and_22_out, and_23_out, and_24_out, and_25_out,
       and_26_out, and_27_out, and_28_out, and_29_out, and_30_out, and_31_out, and_32_out, and_33_out,
       and_34_out, and_35_out, and_36_out, and_37_out, and_38_out, and_39_out, and_40_out, and_41_out,
       and_42_out, and_43_out, and_44_out, and_45_out, and_46_out, and_47_out, and_48_out, and_49_out,
       and_50_out, and_51_out, and_52_out, and_53_out, and_54_out, and_55_out, and_56_out, and_57_out,
       and_58_out, and_59_out, and_60_out, and_61_out, and_62_out, and_63_out, and_64_out, and_65_out,
       and_66_out, and_67_out, and_68_out, and_69_out, and_70_out, and_71_out, and_72_out, and_73_out,
       and_74_out, and_75_out, and_76_out, and_77_out, and_78_out, and_79_out, and_80_out, and_81_out,
       and_82_out, and_83_out, and_84_out, and_85_out, and_86_out, and_87_out, and_88_out, and_89_out,
       and_90_out, and_91_out, and_92_out, and_93_out, and_94_out, and_95_out, and_96_out, and_97_out,
       and_98_out, and_99_out, and_100_out, and_101_out, and_102_out, and_103_out, and_104_out, and_105_out,
       and_106_out, and_107_out, and_108_out, and_109_out, and_110_out, and_111_out, and_112_out,
       and_113_out, and_114_out, and_115_out, and_116_out, or_1_out, or_2_out, or_3_out, or_4_out, or_5_out,
       or_6_out, or_7_out, or_8_out, or_9_out, or_10_out, or_11_out, or_12_out, or_13_out, or_14_out,
       or_15_out, or_16_out, or_17_out, or_18_out, or_19_out, or_20_out, or_21_out, or_22_out, or_23_out,
       or_24_out, or_25_out, or_26_out, xor_1_out, xor_2_out, xor_3_out, xor_4_out, xor_5_out, xor_6_out,
       xor_7_out, xor_8_out, xor_9_out, xor_10_out, xor_11_out, xor_12_out, xor_13_out, xor_14_out,
       xor_15_out, xor_16_out, xor_17_out, xor_18_out, xor_19_out, xor_20_out, xor_21_out, xor_22_out,
       xor_23_out, xor_24_out, xor_26_out, xor_27_out, xor_28_out, xor_29_out, xor_30_out, xor_31_out,
       xor_32_out, xor_33_out, xor_34_out, xor_35_out, xor_36_out, xor_37_out, xor_38_out, xor_39_out,
       xor_40_out, xor_41_out, xor_42_out, xor_43_out, xor_44_out, xor_45_out, xor_47_out, xor_48_out,
       xor_49_out, xor_51_out;

  and and_1 (and_1_out, b0, a0);
  and and_2 (and_2_out, b0, a0);
  and and_3 (and_3_out, b0, a0);
  and and_4 (and_4_out, b0, a0);
  and and_5 (and_5_out, b0, a0);
  and and_6 (and_6_out, b0, a0);
  and and_7 (and_7_out, b0, a0);
  and and_8 (and_8_out, b0, a0);
  and and_9 (and_9_out, b0, a1);
  and and_10 (and_10_out, b0, a1);
  and and_11 (and_11_out, b0, a1);
  and and_12 (and_12_out, b0, a1);
  and and_13 (and_13_out, b0, a1);
  and and_14 (and_14_out, b0, a1);
  and and_15 (and_15_out, b0, a1);
  and and_16 (and_16_out, b0, a1);
  and and_17 (and_17_out, b0, a2);
  and and_18 (and_18_out, b0, a2);
  and and_19 (and_19_out, b0, a2);
  and and_20 (and_20_out, b0, a2);
  and and_21 (and_21_out, b0, a2);
  and and_22 (and_22_out, b0, a2);
  and and_23 (and_23_out, b0, a2);
  and and_24 (and_24_out, b0, a2);
  and and_25 (and_25_out, b0, a3);
  and and_26 (and_26_out, b0, a3);
  and and_27 (and_27_out, b0, a3);
  and and_28 (and_28_out, b0, a3);
  and and_29 (and_29_out, b0, a3);
  and and_30 (and_30_out, b0, a3);
  and and_31 (and_31_out, b0, a3);
  and and_32 (and_32_out, b0, a3);
  and and_33 (and_33_out, b0, a4);
  and and_34 (and_34_out, b0, a4);
  and and_35 (and_35_out, b0, a4);
  and and_36 (and_36_out, b0, a4);
  and and_37 (and_37_out, b0, a4);
  and and_38 (and_38_out, b0, a4);
  and and_39 (and_39_out, b0, a4);
  and and_40 (and_40_out, b0, a4);
  and and_41 (and_41_out, b0, a5);
  and and_42 (and_42_out, b0, a5);
  and and_43 (and_43_out, b0, a5);
  and and_44 (and_44_out, b0, a5);
  and and_45 (and_45_out, b0, a5);
  and and_46 (and_46_out, b0, a5);
  and and_47 (and_47_out, b0, a5);
  and and_48 (and_48_out, b0, a5);
  and and_49 (and_49_out, b0, a6);
  and and_50 (and_50_out, b0, a6);
  and and_51 (and_51_out, b0, a6);
  and and_52 (and_52_out, b0, a6);
  and and_53 (and_53_out, b0, a6);
  and and_54 (and_54_out, b0, a6);
  and and_55 (and_55_out, b0, a6);
  and and_56 (and_56_out, b0, a6);
  and and_57 (and_57_out, b0, b0);
  and and_58 (and_58_out, b0, b0);
  and and_59 (and_59_out, b0, b0);
  and and_60 (and_60_out, b0, b0);
  and and_61 (and_61_out, b0, b0);
  and and_62 (and_62_out, b0, b0);
  and and_63 (and_63_out, b0, b0);
  and and_64 (and_64_out, b0, b0);
  xor xor_1 (xor_1_out, and_16_out, and_23_out);
  and and_65 (and_65_out, and_23_out, and_16_out);
  xor xor_2 (xor_2_out, and_44_out, and_51_out);
  and and_66 (and_66_out, and_51_out, and_44_out);
  xor xor_3 (xor_3_out, xor_1_out, and_30_out);
  and and_67 (and_67_out, and_30_out, xor_1_out);
  xor xor_4 (xor_4_out, xor_2_out, and_58_out);
  and and_68 (and_68_out, and_58_out, xor_2_out);
  xor xor_5 (xor_5_out, xor_3_out, and_37_out);
  and and_69 (and_69_out, and_37_out, xor_3_out);
  xor xor_6 (xor_6_out, xor_4_out, x4);
  and and_70 (and_70_out, x4, xor_4_out);
  xor xor_7 (xor_7_out, xor_5_out, Cin);
  and and_71 (and_71_out, Cin, xor_5_out);
  xor xor_8 (xor_8_out, xor_6_out, Cin_3);
  and and_72 (and_72_out, Cin_3, xor_6_out);
  or or_1 (or_1_out, and_67_out, and_69_out, and_71_out);
  or or_2 (or_2_out, and_67_out, and_65_out);
  or or_3 (or_3_out, and_68_out, and_70_out, and_72_out);
  or or_4 (or_4_out, and_68_out, and_66_out);
  xor xor_9 (xor_9_out, xor_7_out, xor_8_out);
  and and_73 (and_73_out, xor_7_out, xor_8_out);
  xor xor_10 (xor_10_out, xor_9_out, cin_2);
  and and_74 (and_74_out, xor_9_out, cin_2);
  or or_5 (or_5_out, and_74_out, and_73_out);
  xor xor_11 (xor_11_out, and_24_out, and_31_out);
  and and_75 (and_75_out, and_31_out, and_24_out);
  xor xor_12 (xor_12_out, and_52_out, and_59_out);
  and and_76 (and_76_out, and_59_out, and_52_out);
  xor xor_13 (xor_13_out, xor_11_out, and_38_out);
  and and_77 (and_77_out, and_38_out, xor_11_out);
  xor xor_14 (xor_14_out, xor_12_out, or_2_out);
  and and_78 (and_78_out, or_2_out, xor_12_out);
  xor xor_15 (xor_15_out, xor_13_out, and_45_out);
  and and_79 (and_79_out, and_45_out, xor_13_out);
  xor xor_16 (xor_16_out, xor_14_out, or_3_out);
  and and_80 (and_80_out, or_3_out, xor_14_out);
  xor xor_17 (xor_17_out, xor_15_out, or_1_out);
  and and_81 (and_81_out, or_1_out, xor_15_out);
  xor xor_18 (xor_18_out, xor_16_out, or_4_out);
  and and_82 (and_82_out, or_4_out, xor_16_out);
  or or_6 (or_6_out, and_77_out, and_79_out, and_81_out);
  or or_7 (or_7_out, and_77_out, and_75_out);
  or or_8 (or_8_out, and_78_out, and_80_out, and_82_out);
  or or_9 (or_9_out, and_78_out, and_76_out);
  xor xor_19 (xor_19_out, xor_17_out, xor_18_out);
  and and_83 (and_83_out, xor_18_out, xor_17_out);
  xor xor_20 (xor_20_out, xor_19_out, or_5_out);
  and and_84 (and_84_out, or_5_out, xor_19_out);
  and and_85 (and_85_out, and_39_out, and_32_out);
  xor xor_21 (xor_21_out, xor_20_out, x4_2);
  and and_86 (and_86_out, x4_2, xor_20_out);
  xor xor_22 (xor_22_out, and_32_out, and_39_out);
  xor xor_23 (xor_23_out, and_60_out, or_7_out);
  and and_87 (and_87_out, or_7_out, and_60_out);
  xor xor_24 (xor_24_out, xor_22_out, and_46_out);
  and and_88 (and_88_out, and_46_out, xor_22_out);
  // XOR_Gate xor_25 has open pins: in0=xor_21_out, in1=Cin_4, out=open
  and and_89 (and_89_out, Cin_4, xor_21_out);
  xor xor_26 (xor_26_out, xor_23_out, or_8_out);
  and and_90 (and_90_out, or_8_out, xor_23_out);
  or or_10 (or_10_out, and_84_out, and_86_out, and_89_out);
  or or_11 (or_11_out, and_84_out, and_83_out);
  xor xor_27 (xor_27_out, xor_24_out, and_53_out);
  and and_91 (and_91_out, and_53_out, xor_24_out);
  xor xor_28 (xor_28_out, xor_26_out, or_9_out);
  and and_92 (and_92_out, or_9_out, xor_26_out);
  xor xor_29 (xor_29_out, xor_27_out, or_6_out);
  and and_93 (and_93_out, or_6_out, xor_27_out);
  xor xor_30 (xor_30_out, xor_28_out, or_10_out);
  and and_94 (and_94_out, or_10_out, xor_28_out);
  or or_12 (or_12_out, and_88_out, and_91_out, and_93_out);
  or or_13 (or_13_out, and_88_out, and_85_out);
  or or_14 (or_14_out, and_90_out, and_92_out, and_94_out);
  or or_15 (or_15_out, and_90_out, and_87_out);
  xor xor_31 (xor_31_out, xor_29_out, xor_30_out);
  and and_95 (and_95_out, xor_29_out, xor_30_out);
  xor xor_32 (xor_32_out, and_40_out, and_47_out);
  and and_96 (and_96_out, and_47_out, and_40_out);
  xor xor_33 (xor_33_out, xor_31_out, or_11_out);
  and and_97 (and_97_out, xor_31_out, or_11_out);
  or or_16 (or_16_out, and_97_out, and_95_out);
  xor xor_34 (xor_34_out, xor_32_out, and_54_out);
  and and_98 (and_98_out, and_54_out, xor_32_out);
  xor xor_35 (xor_35_out, or_13_out, or_14_out);
  and and_99 (and_99_out, or_13_out, or_14_out);
  xor xor_36 (xor_36_out, xor_34_out, and_61_out);
  and and_100 (and_100_out, and_61_out, xor_34_out);
  xor xor_37 (xor_37_out, xor_35_out, or_15_out);
  and and_101 (and_101_out, xor_35_out, or_15_out);
  xor xor_38 (xor_38_out, xor_36_out, or_12_out);
  and and_102 (and_102_out, or_12_out, xor_36_out);
  or or_17 (or_17_out, and_101_out, and_99_out);
  or or_18 (or_18_out, and_98_out, and_100_out, and_102_out);
  or or_19 (or_19_out, and_98_out, and_96_out);
  xor xor_39 (xor_39_out, xor_38_out, xor_37_out);
  and and_103 (and_103_out, xor_38_out, xor_37_out);
  xor xor_40 (xor_40_out, xor_39_out, or_16_out);
  and and_104 (and_104_out, xor_39_out, or_16_out);
  or or_20 (or_20_out, and_104_out, and_103_out);
  xor xor_41 (xor_41_out, and_48_out, and_55_out);
  and and_105 (and_105_out, and_55_out, and_48_out);
  xor xor_42 (xor_42_out, xor_41_out, and_62_out);
  and and_106 (and_106_out, and_62_out, xor_41_out);
  and and_107 (and_107_out, or_18_out, xor_42_out);
  xor xor_43 (xor_43_out, xor_42_out, or_18_out);
  xor xor_44 (xor_44_out, xor_43_out, or_19_out);
  and and_108 (and_108_out, or_19_out, xor_43_out);
  or or_21 (or_21_out, and_106_out, and_107_out, and_108_out);
  or or_22 (or_22_out, and_106_out, and_105_out);
  xor xor_45 (xor_45_out, xor_44_out, or_17_out);
  and and_109 (and_109_out, xor_44_out, or_17_out);
  // XOR_Gate xor_46 has open pins: in0=xor_45_out, in1=or_20_out, out=open
  and and_110 (and_110_out, xor_45_out, or_20_out);
  or or_23 (or_23_out, and_110_out, and_109_out);
  xor xor_47 (xor_47_out, and_56_out, and_63_out);
  and and_111 (and_111_out, and_63_out, and_56_out);
  xor xor_48 (xor_48_out, xor_47_out, or_21_out);
  and and_112 (and_112_out, or_21_out, xor_47_out);
  xor xor_49 (xor_49_out, xor_48_out, or_22_out);
  and and_113 (and_113_out, or_22_out, xor_48_out);
  // XOR_Gate xor_50 has open pins: in0=xor_49_out, in1=or_23_out, out=open
  and and_114 (and_114_out, or_23_out, xor_49_out);
  or or_24 (or_24_out, and_112_out, and_113_out, and_114_out);
  or or_25 (or_25_out, and_112_out, and_111_out);
  xor xor_51 (xor_51_out, and_64_out, or_24_out);
  and and_115 (and_115_out, and_64_out, or_24_out);
  // XOR_Gate xor_52 has open pins: in0=xor_51_out, in1=or_25_out, out=open
  and and_116 (and_116_out, xor_51_out, or_25_out);
  or or_26 (or_26_out, and_116_out, and_115_out);

  assign b1 = b0;
  assign b2 = b0;
  assign b3 = b0;
  assign b4 = b0;
  assign b5 = b0;
  assign b6 = b0;
  assign b7 = b0;
  assign b7_2 = b0;

  // Notes on the sheet:
  //   a0
  //   a1
  //   a2
  //   a3
  //   a4
  //   a5
  //   a6
  //   a7
  //   0
  //   1
  //   2
  //   3
  //   4
  //   5
  //   6
  //   7
  //   8
  //   9
  //   10
  //   11
  //   12
  //   13
  //   14
  //   x1
  //   x2
  //   x3
  //   x4
  //   x1
  //   x2
  //   x3
  //   t1
  //   t2
  //   t1
  //   t2
  //   t3
  //   t4
  //   KOMPRESOR B
  //   t3
  //   t4
  //   KOMPRESOR A
  //   t6
  //   t5
  //   t5
  //   t6
  //   Sum
  //   c_int
  //   Sum
  //   c_int
  //   Carry
  //   Cout
  //   Carry
  //   Cout
  //   A
  //   B
  //   tutaj cin to bedzie z pierwszego ora z ecm
  //   S1
  //   C1
  //   S
  //   bit 8 wyniku
  //   Cout
  //   do kolumny 9
  //   x1
  //   x2
  //   x3
  //   x4
  //   CIN (carry komp a)
  //   x1
  //   x2
  //   x3
  //   x4
  //   Cin
  //   t1
  //   t2
  //   t1
  //   t2
  //   t3
  //   t4
  //   t3
  //   t4
  //   KOMPRESOR D
  //   KOMPRESOR C
  //   t6
  //   t5
  //   t5
  //   t6
  //   Sum
  //   c_int
  //   Sum
  //   c_int
  //   Carry
  //   Cout
  //   Carry
  //   Cout
  //   x1
  //   x2
  //   x3
  //   tu cin bedzie z 2 ora z ecm
  //   t1
  //   t2
  //   x2
  //   x3
  //   x4
  //   Cin
  //   x1
  //   x1
  //   x2
  //   x3
  //   x4
  //   Cin
  //   t3
  //   t4
  //   t1
  //   t2
  //   t1
  //   t2
  //   t5
  //   t6
  //   TUTAJ KOMPRESOR ZAMIAST SUMATORA WYJATKOWO
  //   t4
  //   BIT 9 WYNIKOWY
  //   Sum
  //   c_int
  //   t3
  //   t3
  //   t4
  //   KOMPRESOR E
  //   KOMPRESOR F
  //   Carry
  //   Cout
  //   t5
  //   t6
  //   t5
  //   t6
  //   Sum
  //   c_int
  //   Sum
  //   c_int
  //   Carry
  //   Cout
  //   Carry
  //   Cout
  //   A
  //   B
  //   x1
  //   x2
  //   x3
  //   x4
  //   Cin
  //   S1
  //   C1
  //   cin
  //   t1
  //   t2
  //   BIT WYNIKOWY 10 KOLUMNY
  //   S
  //   Cout
  //   A
  //   B
  //   t3
  //   t4
  //   S1
  //   C1
  //   t5
  //   t6
  //   cin
  //   KOMPRESOR G
  //   S
  //   Sum
  //   c_int
  //   Cout
  //   Carry
  //   Cout
  //   B
  //   A
  //   S1
  //   C1
  //   cin
  //   BIT 11 WYNIKU
  //   S
  //   x1
  //   x2
  //   x3
  //   x4
  //   Cin
  //   Cout
  //   t1
  //   t2
  //   t3
  //   t4
  //   t5
  //   t6
  //   KOMPRESOR H
  //   Sum
  //   c_int
  //   Carry
  //   Cout
  //   A
  //   B
  //   S1
  //   C1
  //   cin
  //   Sum
  //   BIT 12 WYNIKU
  //   Cout
  //   x1
  //   x2
  //   x3
  //   x4
  //   Cin
  //   t1
  //   t2
  //   t3
  //   t4
  //   KOMPRESOR I
  //   t5
  //   t6
  //   BIT 13 WYNIKU
  //   Sum
  //   c_int
  //   Carry
  //   Cout
  //   A
  //   B
  //   S1
  //   C1
  //   cin
  //   BIT 14 WYNIKU
  //   Sum
  //   Cout
  //   BIT 15 WYNIKU
endmodule

module uklad_koncowy_2 (
  input  a0,
  input  a1,
  input  a2,
  input  a3,
  input  a4,
  input  a5,
  input  a6,
  input  b7,
  input  b0,
  input  b1,
  input  b2,
  input  b3,
  input  b4,
  input  b5,
  input  b6,
  input  b7_2,
  input  Cin,
  input  x4,
  input  Cin_2,
  input  x4_2,
  output out_21,
  output out_22,
  output out_23,
  output out_24,
  output out_25,
  output out_26,
  output out_27,
  output out_28,
  output out_29,
  output out_30,
  output out_31,
  output out_32,
  output out_33,
  output out_34,
  output out_35
);

  wire and_1_out, and_2_out, and_3_out, and_4_out, and_5_out, and_6_out, and_7_out, and_8_out, and_9_out,
       and_10_out, and_11_out, and_12_out, and_13_out, and_14_out, and_15_out, and_16_out, and_17_out,
       and_18_out, and_19_out, and_20_out, and_21_out, and_22_out, and_23_out, and_24_out, and_25_out,
       and_26_out, and_27_out, and_28_out, and_29_out, and_30_out, and_31_out, and_32_out, and_33_out,
       and_34_out, and_35_out, and_36_out, and_37_out, and_38_out, and_39_out, and_40_out, and_41_out,
       and_42_out, and_43_out, and_44_out, and_45_out, and_46_out, and_47_out, and_48_out, and_49_out,
       and_50_out, and_51_out, and_52_out, and_53_out, and_54_out, and_55_out, and_56_out, and_57_out,
       and_58_out, and_59_out, and_60_out, and_61_out, and_62_out, and_63_out, and_64_out, and_65_out,
       and_66_out, and_67_out, and_68_out, and_69_out, and_70_out, and_71_out, and_72_out, and_73_out,
       and_74_out, and_75_out, and_76_out, and_77_out, and_78_out, and_79_out, and_80_out, and_81_out,
       and_82_out, and_83_out, and_84_out, or_1_out, or_2_out, or_3_out, or_4_out, or_5_out, or_6_out,
       or_7_out, or_8_out, or_9_out, or_10_out, or_11_out, or_12_out, or_13_out, or_14_out, or_15_out,
       or_16_out, or_17_out, or_18_out, or_19_out, or_20_out, or_21_out, or_22_out, or_23_out, or_24_out,
       or_25_out, or_26_out, or_27_out, xor_1_out, xor_2_out, xor_3_out, xor_4_out, xor_5_out, xor_6_out,
       xor_7_out, xor_8_out, xor_9_out, xor_11_out, xor_12_out, xor_13_out, xor_14_out, xor_15_out,
       xor_16_out, xor_17_out, xor_18_out, xor_19_out, xor_20_out, xor_21_out, xor_22_out, xor_23_out,
       xor_24_out, xor_26_out, xor_27_out, xor_28_out, xor_29_out, xor_30_out, xor_31_out, xor_33_out,
       xor_34_out, xor_35_out, xor_36_out, xor_37_out, xor_38_out, xor_39_out, xor_41_out, xor_42_out,
       xor_43_out, xor_44_out, xor_45_out, xor_47_out, xor_48_out, xor_49_out, xor_51_out;

  and and_1 (and_1_out, b0, a0);
  and and_2 (and_2_out, b0, a1);
  and and_3 (and_3_out, b0, a1);
  and and_4 (and_4_out, b0, a2);
  and and_5 (and_5_out, b0, a2);
  and and_6 (and_6_out, b0, a2);
  and and_7 (and_7_out, b0, a2);
  and and_8 (and_8_out, b0, a2);
  and and_9 (and_9_out, b0, a2);
  and and_10 (and_10_out, b0, a2);
  and and_11 (and_11_out, b0, a2);
  and and_12 (and_12_out, b0, a2);
  and and_13 (and_13_out, b0, a2);
  and and_14 (and_14_out, b0, a2);
  and and_15 (and_15_out, b0, a5);
  and and_16 (and_16_out, b0, a5);
  and and_17 (and_17_out, b0, a5);
  and and_18 (and_18_out, b0, a5);
  and and_19 (and_19_out, b0, a5);
  and and_20 (and_20_out, b0, a6);
  and and_21 (and_21_out, b0, a6);
  and and_22 (and_22_out, b0, a6);
  and and_23 (and_23_out, b0, a6);
  and and_24 (and_24_out, b0, a6);
  and and_25 (and_25_out, b0, a6);
  and and_26 (and_26_out, b0, b0);
  and and_27 (and_27_out, b0, b0);
  and and_28 (and_28_out, b0, b0);
  and and_29 (and_29_out, b0, b0);
  and and_30 (and_30_out, b0, b0);
  and and_31 (and_31_out, b0, b0);
  and and_32 (and_32_out, b0, b0);
  or or_1 (or_1_out, and_1_out, and_2_out, and_4_out, and_7_out);
  or or_2 (or_2_out, and_11_out, and_15_out, and_20_out, and_26_out);
  xor xor_1 (xor_1_out, and_3_out, and_5_out);
  and and_33 (and_33_out, and_5_out, and_3_out);
  xor xor_2 (xor_2_out, and_15_out, and_20_out);
  and and_34 (and_34_out, and_20_out, and_15_out);
  xor xor_3 (xor_3_out, xor_1_out, and_8_out);
  and and_35 (and_35_out, and_8_out, xor_1_out);
  xor xor_4 (xor_4_out, xor_2_out, and_26_out);
  and and_36 (and_36_out, and_26_out, xor_2_out);
  xor xor_5 (xor_5_out, xor_3_out, and_11_out);
  and and_37 (and_37_out, and_11_out, xor_3_out);
  xor xor_6 (xor_6_out, xor_4_out, x4);
  and and_38 (and_38_out, x4, xor_4_out);
  xor xor_7 (xor_7_out, xor_5_out, Cin);
  and and_39 (and_39_out, Cin, xor_5_out);
  xor xor_8 (xor_8_out, xor_6_out, Cin_2);
  and and_40 (and_40_out, Cin_2, xor_6_out);
  or or_3 (or_3_out, and_35_out, and_37_out, and_39_out);
  or or_4 (or_4_out, and_35_out, and_33_out);
  or or_5 (or_5_out, and_36_out, and_38_out, and_40_out);
  or or_6 (or_6_out, and_36_out, and_34_out);
  xor xor_9 (xor_9_out, xor_7_out, xor_8_out);
  and and_41 (and_41_out, xor_7_out, xor_8_out);
  xor xor_10 (out_28, xor_9_out, or_1_out);
  and and_42 (and_42_out, xor_9_out, or_1_out);
  or or_7 (or_7_out, and_42_out, and_41_out);
  xor xor_11 (xor_11_out, and_6_out, and_9_out);
  and and_43 (and_43_out, and_9_out, and_6_out);
  xor xor_12 (xor_12_out, and_21_out, and_27_out);
  and and_44 (and_44_out, and_27_out, and_21_out);
  xor xor_13 (xor_13_out, xor_11_out, and_12_out);
  and and_45 (and_45_out, and_12_out, xor_11_out);
  xor xor_14 (xor_14_out, xor_12_out, or_4_out);
  and and_46 (and_46_out, or_4_out, xor_12_out);
  xor xor_15 (xor_15_out, xor_13_out, and_16_out);
  and and_47 (and_47_out, and_16_out, xor_13_out);
  xor xor_16 (xor_16_out, xor_14_out, or_5_out);
  and and_48 (and_48_out, or_5_out, xor_14_out);
  xor xor_17 (xor_17_out, xor_15_out, or_3_out);
  and and_49 (and_49_out, or_3_out, xor_15_out);
  xor xor_18 (xor_18_out, xor_16_out, or_6_out);
  and and_50 (and_50_out, or_6_out, xor_16_out);
  or or_8 (or_8_out, and_45_out, and_47_out, and_49_out);
  or or_9 (or_9_out, and_45_out, and_43_out);
  or or_10 (or_10_out, and_46_out, and_48_out, and_50_out);
  or or_11 (or_11_out, and_46_out, and_44_out);
  xor xor_19 (xor_19_out, xor_17_out, xor_18_out);
  and and_51 (and_51_out, xor_18_out, xor_17_out);
  xor xor_20 (xor_20_out, xor_19_out, or_7_out);
  and and_52 (and_52_out, or_7_out, xor_19_out);
  xor xor_21 (xor_21_out, and_10_out, and_13_out);
  and and_53 (and_53_out, and_13_out, and_10_out);
  xor xor_22 (xor_22_out, xor_20_out, x4_2);
  and and_54 (and_54_out, x4_2, xor_20_out);
  xor xor_23 (xor_23_out, and_28_out, or_9_out);
  and and_55 (and_55_out, or_9_out, and_28_out);
  xor xor_24 (xor_24_out, xor_21_out, and_17_out);
  and and_56 (and_56_out, and_17_out, xor_21_out);
  xor xor_25 (out_27, xor_22_out, or_2_out);
  and and_57 (and_57_out, or_2_out, xor_22_out);
  xor xor_26 (xor_26_out, xor_23_out, or_10_out);
  and and_58 (and_58_out, or_10_out, xor_23_out);
  xor xor_27 (xor_27_out, xor_24_out, and_22_out);
  and and_59 (and_59_out, and_22_out, xor_24_out);
  or or_12 (or_12_out, and_52_out, and_54_out, and_57_out);
  or or_13 (or_13_out, and_52_out, and_51_out);
  xor xor_28 (xor_28_out, xor_26_out, or_11_out);
  and and_60 (and_60_out, or_11_out, xor_26_out);
  xor xor_29 (xor_29_out, xor_27_out, or_8_out);
  and and_61 (and_61_out, or_8_out, xor_27_out);
  xor xor_30 (xor_30_out, xor_28_out, or_12_out);
  and and_62 (and_62_out, or_12_out, xor_28_out);
  or or_14 (or_14_out, and_56_out, and_59_out, and_61_out);
  or or_15 (or_15_out, and_56_out, and_53_out);
  or or_16 (or_16_out, and_58_out, and_60_out, and_62_out);
  or or_17 (or_17_out, and_58_out, and_55_out);
  xor xor_31 (xor_31_out, xor_29_out, xor_30_out);
  and and_63 (and_63_out, xor_29_out, xor_30_out);
  xor xor_32 (out_26, xor_31_out, or_13_out);
  and and_64 (and_64_out, xor_31_out, or_13_out);
  xor xor_33 (xor_33_out, and_14_out, and_18_out);
  and and_65 (and_65_out, and_18_out, and_14_out);
  or or_18 (or_18_out, and_64_out, and_63_out);
  xor xor_34 (xor_34_out, xor_33_out, and_23_out);
  and and_66 (and_66_out, and_23_out, xor_33_out);
  xor xor_35 (xor_35_out, or_15_out, or_16_out);
  and and_67 (and_67_out, or_15_out, or_16_out);
  xor xor_36 (xor_36_out, xor_34_out, and_29_out);
  and and_68 (and_68_out, and_29_out, xor_34_out);
  and and_69 (and_69_out, xor_35_out, or_17_out);
  xor xor_37 (xor_37_out, xor_36_out, or_14_out);
  and and_70 (and_70_out, or_14_out, xor_36_out);
  xor xor_38 (xor_38_out, xor_35_out, or_17_out);
  or or_19 (or_19_out, and_69_out, and_67_out);
  or or_20 (or_20_out, and_66_out, and_68_out, and_70_out);
  or or_21 (or_21_out, and_66_out, and_65_out);
  xor xor_39 (xor_39_out, xor_37_out, xor_38_out);
  and and_71 (and_71_out, xor_37_out, xor_38_out);
  xor xor_40 (out_25, xor_39_out, or_18_out);
  and and_72 (and_72_out, xor_39_out, or_18_out);
  or or_22 (or_22_out, and_72_out, and_71_out);
  xor xor_41 (xor_41_out, and_19_out, and_24_out);
  and and_73 (and_73_out, and_24_out, and_19_out);
  xor xor_42 (xor_42_out, xor_41_out, and_30_out);
  and and_74 (and_74_out, and_30_out, xor_41_out);
  xor xor_43 (xor_43_out, xor_42_out, or_20_out);
  and and_75 (and_75_out, or_20_out, xor_42_out);
  xor xor_44 (xor_44_out, xor_43_out, or_21_out);
  and and_76 (and_76_out, or_21_out, xor_43_out);
  or or_23 (or_23_out, and_74_out, and_75_out, and_76_out);
  or or_24 (or_24_out, and_74_out, and_73_out);
  xor xor_45 (xor_45_out, xor_44_out, or_19_out);
  and and_77 (and_77_out, xor_44_out, or_19_out);
  xor xor_46 (out_24, xor_45_out, or_22_out);
  and and_78 (and_78_out, xor_45_out, or_22_out);
  or or_25 (or_25_out, and_78_out, and_77_out);
  xor xor_47 (xor_47_out, and_25_out, and_31_out);
  and and_79 (and_79_out, and_31_out, and_25_out);
  and and_80 (and_80_out, or_23_out, xor_47_out);
  xor xor_48 (xor_48_out, xor_47_out, or_23_out);
  xor xor_49 (xor_49_out, xor_48_out, or_24_out);
  and and_81 (and_81_out, or_24_out, xor_48_out);
  and and_82 (and_82_out, or_25_out, xor_49_out);
  xor xor_50 (out_23, xor_49_out, or_25_out);
  or or_26 (or_26_out, and_80_out, and_81_out, and_82_out);
  or or_27 (or_27_out, and_80_out, and_79_out);
  xor xor_51 (xor_51_out, and_32_out, or_26_out);
  and and_83 (and_83_out, and_32_out, or_26_out);
  xor xor_52 (out_22, xor_51_out, or_27_out);
  and and_84 (and_84_out, xor_51_out, or_27_out);
  or or_28 (out_21, and_84_out, and_83_out);

  assign a3 = a2;
  assign a4 = a2;
  assign b1 = b0;
  assign b2 = b0;
  assign b3 = b0;
  assign b4 = b0;
  assign b5 = b0;
  assign b6 = b0;
  assign b7 = b0;
  assign b7_2 = b0;
  assign out_29 = 1'b0;
  assign out_30 = 1'b0;
  assign out_31 = 1'b0;
  assign out_32 = 1'b0;
  assign out_33 = 1'b0;
  assign out_34 = 1'b1;
  assign out_35 = 1'b0;

  // Notes on the sheet:
  //   a0
  //   a1
  //   a2
  //   a3
  //   a4
  //   a5
  //   a6
  //   a7
  //   0
  //   1
  //   2
  //   3
  //   4
  //   5
  //   7
  //   9
  //   11
  //   12
  //   13
  //   14
  //   6
  //   8
  //   10
  //   Carry_8
  //   Carry_9
  //   x1
  //   x2
  //   x3
  //   x4
  //   x1
  //   x2
  //   x3
  //   t1
  //   t2
  //   t1
  //   t2
  //   t3
  //   t4
  //   t4
  //   KOMPRESOR B
  //   KOMPRESOR A
  //   t3
  //   t5
  //   t6
  //   t5
  //   t6
  //   Sum
  //   c_int
  //   Sum
  //   c_int
  //   Carry
  //   Cout
  //   Carry
  //   Cout
  //   B
  //   A
  //   S1
  //   C1
  //   tutaj cin to bedzie z pierwszego ora z ecm
  //   cin
  //   S
  //   bit 8 wyniku
  //   Cout
  //   do kolumny 9
  //   x1
  //   x2
  //   x3
  //   x4
  //   CIN (carry komp a)
  //   Cin
  //   x1
  //   x2
  //   x3
  //   x4
  //   t1
  //   t2
  //   t1
  //   t2
  //   t3
  //   t4
  //   t4
  //   t3
  //   KOMPRESOR D
  //   KOMPRESOR C
  //   t5
  //   t6
  //   t5
  //   t6
  //   Sum
  //   c_int
  //   Sum
  //   c_int
  //   Carry
  //   Cout
  //   Carry
  //   Cout
  //   x1
  //   x2
  //   x3
  //   Cin
  //   tu cin bedzie z 2 ora z ecm
  //   t1
  //   t2
  //   x1
  //   x2
  //   x3
  //   x4
  //   Cin
  //   x1
  //   x2
  //   x3
  //   x4
  //   Cin
  //   t3
  //   t4
  //   t1
  //   t2
  //   t5
  //   t6
  //   t1
  //   t2
  //   TUTAJ KOMPRESOR ZAMIAST SUMATORA WYJATKOWO
  //   BIT 9 WYNIKOWY
  //   t3
  //   t4
  //   Sum
  //   c_int
  //   t3
  //   t4
  //   KOMPRESOR E
  //   KOMPRESOR F
  //   Carry
  //   Cout
  //   t5
  //   t6
  //   t5
  //   t6
  //   Sum
  //   c_int
  //   Sum
  //   c_int
  //   Carry
  //   Cout
  //   Carry
  //   Cout
  //   A
  //   B
  //   x1
  //   x2
  //   x3
  //   x4
  //   Cin
  //   cin
  //   S1
  //   C1
  //   t1
  //   BIT WYNIKOWY 10 KOLUMNY
  //   S
  //   t2
  //   Cout
  //   t4
  //   A
  //   B
  //   t3
  //   S1
  //   C1
  //   KOMPRESOR G
  //   t5
  //   t6
  //   cin
  //   Sum
  //   c_int
  //   S
  //   Cout
  //   Carry
  //   Cout
  //   A
  //   B
  //   S1
  //   C1
  //   cin
  //   BIT 11 WYNIKU
  //   S
  //   x1
  //   x2
  //   x3
  //   x4
  //   Cin
  //   Cout
  //   t1
  //   t2
  //   t3
  //   t4
  //   t6
  //   KOMPRESOR H
  //   t5
  //   Sum
  //   c_int
  //   Carry
  //   Cout
  //   A
  //   B
  //   S1
  //   C1
  //   cin
  //   BIT 12 WYNIKU
  //   Sum
  //   Cout
  //   x1
  //   x2
  //   x3
  //   x4
  //   Cin
  //   t1
  //   t2
  //   t3
  //   t4
  //   KOMPRESOR I
  //   t5
  //   t6
  //   BIT 13 WYNIKU
  //   Sum
  //   c_int
  //   Carry
  //   Cout
  //   A
  //   B
  //   S1
  //   C1
  //   cin
  //   BIT 14 WYNIKU
  //   Sum
  //   Cout
  //   BIT 15 WYNIKU
endmodule

module uklad_koncowy_3 (
  input  a0,
  input  a1,
  input  a2,
  input  a3,
  input  a4,
  input  a5,
  input  a6,
  input  a7,
  input  b0,
  input  b1,
  input  b2,
  input  b3,
  input  b4,
  input  b5,
  input  b6,
  input  b7,
  input  x4,
  output out_18,
  output out_19,
  output out_20,
  output out_21,
  output out_22,
  output out_23,
  output out_24,
  output out_25,
  output out_26,
  output out_27,
  output out_28,
  output out_29,
  output out_30,
  output out_31,
  output out_32,
  output out_33
);

  wire and_1_out, and_2_out, and_3_out, and_4_out, and_5_out, and_6_out, and_7_out, and_8_out, and_9_out,
       and_10_out, and_11_out, and_12_out, and_13_out, and_14_out, and_15_out, and_16_out, and_17_out,
       and_18_out, and_19_out, and_20_out, and_21_out, and_22_out, and_23_out, and_24_out, and_25_out,
       and_26_out, and_27_out, and_28_out, and_29_out, and_30_out, and_31_out, and_32_out, and_33_out,
       and_34_out, and_35_out, and_36_out, and_37_out, and_38_out, and_39_out, and_40_out, and_41_out,
       and_42_out, and_43_out, and_44_out, and_45_out, and_46_out, and_47_out, and_48_out, and_49_out,
       and_50_out, and_51_out, and_52_out, and_53_out, and_54_out, and_55_out, and_56_out, and_57_out,
       and_58_out, and_59_out, and_60_out, and_61_out, and_62_out, and_63_out, and_64_out, and_65_out,
       and_66_out, and_67_out, and_68_out, and_69_out, and_70_out, and_71_out, and_72_out, and_73_out,
       and_74_out, and_75_out, and_76_out, and_77_out, and_78_out, and_79_out, and_80_out, and_81_out,
       and_82_out, and_83_out, and_84_out, or_1_out, or_2_out, or_3_out, or_4_out, or_5_out, or_6_out,
       or_7_out, or_8_out, or_9_out, or_10_out, or_11_out, or_12_out, or_13_out, or_14_out, or_15_out,
       or_16_out, or_17_out, or_18_out, or_19_out, or_20_out, or_21_out, or_22_out, or_23_out, or_24_out,
       or_25_out, or_26_out, or_27_out, xor_1_out, xor_2_out, xor_3_out, xor_4_out, xor_5_out, xor_6_out,
       xor_7_out, xor_8_out, xor_9_out, xor_11_out, xor_12_out, xor_13_out, xor_14_out, xor_15_out,
       xor_16_out, xor_17_out, xor_18_out, xor_19_out, xor_20_out, xor_21_out, xor_22_out, xor_23_out,
       xor_24_out, xor_26_out, xor_27_out, xor_28_out, xor_29_out, xor_30_out, xor_31_out, xor_33_out,
       xor_34_out, xor_35_out, xor_36_out, xor_37_out, xor_38_out, xor_39_out, xor_41_out, xor_42_out,
       xor_43_out, xor_44_out, xor_45_out, xor_47_out, xor_48_out, xor_49_out, xor_51_out;

  and and_1 (and_1_out, b4, a0);
  and and_2 (and_2_out, b3, a1);
  and and_3 (and_3_out, b7, a1);
  and and_4 (and_4_out, b2, a2);
  and and_5 (and_5_out, b6, a2);
  and and_6 (and_6_out, b7, a2);
  and and_7 (and_7_out, b1, a3);
  and and_8 (and_8_out, b5, a3);
  and and_9 (and_9_out, b6, a3);
  and and_10 (and_10_out, b7, a3);
  and and_11 (and_11_out, b4, a4);
  and and_12 (and_12_out, b5, a4);
  and and_13 (and_13_out, b6, a4);
  and and_14 (and_14_out, b7, a4);
  and and_15 (and_15_out, b3, a5);
  and and_16 (and_16_out, b4, a5);
  and and_17 (and_17_out, b5, a5);
  and and_18 (and_18_out, b6, a5);
  and and_19 (and_19_out, b7, a5);
  and and_20 (and_20_out, b2, a6);
  and and_21 (and_21_out, b3, a6);
  and and_22 (and_22_out, b4, a6);
  and and_23 (and_23_out, b5, a6);
  and and_24 (and_24_out, b6, a6);
  and and_25 (and_25_out, b7, a6);
  and and_26 (and_26_out, b1, a7);
  and and_27 (and_27_out, b2, a7);
  and and_28 (and_28_out, b3, a7);
  and and_29 (and_29_out, b4, a7);
  and and_30 (and_30_out, b5, a7);
  and and_31 (and_31_out, b6, a7);
  and and_32 (and_32_out, b7, a7);
  or or_1 (or_1_out, and_1_out, and_2_out, and_4_out, and_7_out);
  or or_2 (or_2_out, and_11_out, and_15_out, and_20_out, and_26_out);
  xor xor_1 (xor_1_out, and_3_out, and_5_out);
  and and_33 (and_33_out, and_5_out, and_3_out);
  xor xor_2 (xor_2_out, and_15_out, and_20_out);
  and and_34 (and_34_out, and_20_out, and_15_out);
  xor xor_3 (xor_3_out, xor_1_out, and_8_out);
  and and_35 (and_35_out, and_8_out, xor_1_out);
  xor xor_4 (xor_4_out, xor_2_out, and_26_out);
  and and_36 (and_36_out, and_26_out, xor_2_out);
  xor xor_5 (xor_5_out, xor_3_out, and_11_out);
  and and_37 (and_37_out, and_11_out, xor_3_out);
  xor xor_6 (xor_6_out, xor_4_out, 1'b0);
  and and_38 (and_38_out, 1'b0, xor_4_out);
  xor xor_7 (xor_7_out, xor_5_out, 1'b0);
  and and_39 (and_39_out, 1'b0, xor_5_out);
  xor xor_8 (xor_8_out, xor_6_out, 1'b0);
  and and_40 (and_40_out, 1'b0, xor_6_out);
  or or_3 (or_3_out, and_35_out, and_37_out, and_39_out);
  or or_4 (or_4_out, and_35_out, and_33_out);
  or or_5 (or_5_out, and_36_out, and_38_out, and_40_out);
  or or_6 (or_6_out, and_36_out, and_34_out);
  xor xor_9 (xor_9_out, xor_7_out, xor_8_out);
  and and_41 (and_41_out, xor_7_out, xor_8_out);
  xor xor_10 (out_25, xor_9_out, or_1_out);
  and and_42 (and_42_out, xor_9_out, or_1_out);
  or or_7 (or_7_out, and_42_out, and_41_out);
  xor xor_11 (xor_11_out, and_6_out, and_9_out);
  and and_43 (and_43_out, and_9_out, and_6_out);
  xor xor_12 (xor_12_out, and_21_out, and_27_out);
  and and_44 (and_44_out, and_27_out, and_21_out);
  xor xor_13 (xor_13_out, xor_11_out, and_12_out);
  and and_45 (and_45_out, and_12_out, xor_11_out);
  xor xor_14 (xor_14_out, xor_12_out, or_4_out);
  and and_46 (and_46_out, or_4_out, xor_12_out);
  xor xor_15 (xor_15_out, xor_13_out, and_16_out);
  and and_47 (and_47_out, and_16_out, xor_13_out);
  xor xor_16 (xor_16_out, xor_14_out, or_5_out);
  and and_48 (and_48_out, or_5_out, xor_14_out);
  xor xor_17 (xor_17_out, xor_15_out, or_3_out);
  and and_49 (and_49_out, or_3_out, xor_15_out);
  xor xor_18 (xor_18_out, xor_16_out, or_6_out);
  and and_50 (and_50_out, or_6_out, xor_16_out);
  or or_8 (or_8_out, and_45_out, and_47_out, and_49_out);
  or or_9 (or_9_out, and_45_out, and_43_out);
  or or_10 (or_10_out, and_46_out, and_48_out, and_50_out);
  or or_11 (or_11_out, and_46_out, and_44_out);
  xor xor_19 (xor_19_out, xor_17_out, xor_18_out);
  and and_51 (and_51_out, xor_18_out, xor_17_out);
  xor xor_20 (xor_20_out, xor_19_out, or_7_out);
  and and_52 (and_52_out, or_7_out, xor_19_out);
  xor xor_21 (xor_21_out, and_10_out, and_13_out);
  and and_53 (and_53_out, and_13_out, and_10_out);
  xor xor_22 (xor_22_out, xor_20_out, x4);
  and and_54 (and_54_out, x4, xor_20_out);
  xor xor_23 (xor_23_out, and_28_out, or_9_out);
  and and_55 (and_55_out, or_9_out, and_28_out);
  xor xor_24 (xor_24_out, xor_21_out, and_17_out);
  and and_56 (and_56_out, and_17_out, xor_21_out);
  xor xor_25 (out_24, xor_22_out, or_2_out);
  and and_57 (and_57_out, or_2_out, xor_22_out);
  xor xor_26 (xor_26_out, xor_23_out, or_10_out);
  and and_58 (and_58_out, or_10_out, xor_23_out);
  xor xor_27 (xor_27_out, xor_24_out, and_22_out);
  and and_59 (and_59_out, and_22_out, xor_24_out);
  or or_12 (or_12_out, and_52_out, and_54_out, and_57_out);
  or or_13 (or_13_out, and_52_out, and_51_out);
  xor xor_28 (xor_28_out, xor_26_out, or_11_out);
  and and_60 (and_60_out, or_11_out, xor_26_out);
  xor xor_29 (xor_29_out, xor_27_out, or_8_out);
  and and_61 (and_61_out, or_8_out, xor_27_out);
  xor xor_30 (xor_30_out, xor_28_out, or_12_out);
  and and_62 (and_62_out, or_12_out, xor_28_out);
  or or_14 (or_14_out, and_56_out, and_59_out, and_61_out);
  or or_15 (or_15_out, and_56_out, and_53_out);
  or or_16 (or_16_out, and_58_out, and_60_out, and_62_out);
  or or_17 (or_17_out, and_58_out, and_55_out);
  xor xor_31 (xor_31_out, xor_29_out, xor_30_out);
  and and_63 (and_63_out, xor_29_out, xor_30_out);
  xor xor_32 (out_23, xor_31_out, or_13_out);
  and and_64 (and_64_out, xor_31_out, or_13_out);
  xor xor_33 (xor_33_out, and_14_out, and_18_out);
  and and_65 (and_65_out, and_18_out, and_14_out);
  or or_18 (or_18_out, and_64_out, and_63_out);
  xor xor_34 (xor_34_out, xor_33_out, and_23_out);
  and and_66 (and_66_out, and_23_out, xor_33_out);
  xor xor_35 (xor_35_out, or_15_out, or_16_out);
  and and_67 (and_67_out, or_15_out, or_16_out);
  xor xor_36 (xor_36_out, xor_34_out, and_29_out);
  and and_68 (and_68_out, and_29_out, xor_34_out);
  and and_69 (and_69_out, xor_35_out, or_17_out);
  xor xor_37 (xor_37_out, xor_36_out, or_14_out);
  and and_70 (and_70_out, or_14_out, xor_36_out);
  xor xor_38 (xor_38_out, xor_35_out, or_17_out);
  or or_19 (or_19_out, and_69_out, and_67_out);
  or or_20 (or_20_out, and_66_out, and_68_out, and_70_out);
  or or_21 (or_21_out, and_66_out, and_65_out);
  xor xor_39 (xor_39_out, xor_37_out, xor_38_out);
  and and_71 (and_71_out, xor_37_out, xor_38_out);
  xor xor_40 (out_22, xor_39_out, or_18_out);
  and and_72 (and_72_out, xor_39_out, or_18_out);
  or or_22 (or_22_out, and_72_out, and_71_out);
  xor xor_41 (xor_41_out, and_19_out, and_24_out);
  and and_73 (and_73_out, and_24_out, and_19_out);
  xor xor_42 (xor_42_out, xor_41_out, and_30_out);
  and and_74 (and_74_out, and_30_out, xor_41_out);
  xor xor_43 (xor_43_out, xor_42_out, or_20_out);
  and and_75 (and_75_out, or_20_out, xor_42_out);
  xor xor_44 (xor_44_out, xor_43_out, or_21_out);
  and and_76 (and_76_out, or_21_out, xor_43_out);
  or or_23 (or_23_out, and_74_out, and_75_out, and_76_out);
  or or_24 (or_24_out, and_74_out, and_73_out);
  xor xor_45 (xor_45_out, xor_44_out, or_19_out);
  and and_77 (and_77_out, xor_44_out, or_19_out);
  xor xor_46 (out_21, xor_45_out, or_22_out);
  and and_78 (and_78_out, xor_45_out, or_22_out);
  or or_25 (or_25_out, and_78_out, and_77_out);
  xor xor_47 (xor_47_out, and_25_out, and_31_out);
  and and_79 (and_79_out, and_31_out, and_25_out);
  and and_80 (and_80_out, or_23_out, xor_47_out);
  xor xor_48 (xor_48_out, xor_47_out, or_23_out);
  xor xor_49 (xor_49_out, xor_48_out, or_24_out);
  and and_81 (and_81_out, or_24_out, xor_48_out);
  and and_82 (and_82_out, or_25_out, xor_49_out);
  xor xor_50 (out_20, xor_49_out, or_25_out);
  or or_26 (or_26_out, and_80_out, and_81_out, and_82_out);
  or or_27 (or_27_out, and_80_out, and_79_out);
  xor xor_51 (xor_51_out, and_32_out, or_26_out);
  and and_83 (and_83_out, and_32_out, or_26_out);
  xor xor_52 (out_19, xor_51_out, or_27_out);
  and and_84 (and_84_out, xor_51_out, or_27_out);
  or or_28 (out_18, and_84_out, and_83_out);

  assign out_26 = 1'b0;
  assign out_27 = 1'b0;
  assign out_28 = 1'b0;
  assign out_29 = 1'b0;
  assign out_30 = 1'b0;
  assign out_31 = 1'b1;
  assign out_32 = 1'b1;
  assign out_33 = 1'b0;

  // Notes on the sheet:
  //   a0
  //   a1
  //   a2
  //   a3
  //   a4
  //   a5
  //   a6
  //   a7
  //   4
  //   9
  //   11
  //   12
  //   13
  //   14
  //   8
  //   10
  //   Carry_8
  //   Carry_9
  //   x1
  //   x2
  //   x3
  //   x4
  //   Cin
  //   x1
  //   x2
  //   x3
  //   x4
  //   Cin
  //   t1
  //   t2
  //   t1
  //   t2
  //   t3
  //   t4
  //   t4
  //   KOMPRESOR B
  //   KOMPRESOR A
  //   t3
  //   t5
  //   t6
  //   t5
  //   t6
  //   Sum
  //   c_int
  //   Sum
  //   c_int
  //   Carry
  //   Cout
  //   Carry
  //   Cout
  //   B
  //   A
  //   S1
  //   C1
  //   tutaj cin to bedzie z pierwszego ora z ecm
  //   cin
  //   S
  //   bit 8 wyniku
  //   Cout
  //   do kolumny 9
  //   x1
  //   x2
  //   x3
  //   x4
  //   CIN (carry komp a)
  //   Cin
  //   x1
  //   x2
  //   x3
  //   x4
  //   t1
  //   t2
  //   t1
  //   t2
  //   t3
  //   t4
  //   t4
  //   t3
  //   KOMPRESOR D
  //   KOMPRESOR C
  //   t5
  //   t6
  //   t5
  //   t6
  //   Sum
  //   c_int
  //   Sum
  //   c_int
  //   Carry
  //   Cout
  //   Carry
  //   Cout
  //   x1
  //   x2
  //   x3
  //   Cin
  //   tu cin bedzie z 2 ora z ecm
  //   t1
  //   t2
  //   x1
  //   x2
  //   x3
  //   x4
  //   Cin
  //   x1
  //   x2
  //   x3
  //   x4
  //   Cin
  //   t3
  //   t4
  //   t1
  //   t2
  //   t5
  //   t6
  //   t1
  //   t2
  //   TUTAJ KOMPRESOR ZAMIAST SUMATORA WYJATKOWO
  //   BIT 9 WYNIKOWY
  //   t3
  //   t4
  //   Sum
  //   c_int
  //   t3
  //   t4
  //   KOMPRESOR E
  //   KOMPRESOR F
  //   Carry
  //   Cout
  //   t5
  //   t6
  //   t5
  //   t6
  //   Sum
  //   c_int
  //   Sum
  //   c_int
  //   Carry
  //   Cout
  //   Carry
  //   Cout
  //   A
  //   B
  //   x1
  //   x2
  //   x3
  //   x4
  //   Cin
  //   cin
  //   S1
  //   C1
  //   t1
  //   BIT WYNIKOWY 10 KOLUMNY
  //   S
  //   t2
  //   Cout
  //   t4
  //   A
  //   B
  //   t3
  //   S1
  //   C1
  //   KOMPRESOR G
  //   t5
  //   t6
  //   cin
  //   Sum
  //   c_int
  //   S
  //   Cout
  //   Carry
  //   Cout
  //   A
  //   B
  //   S1
  //   C1
  //   cin
  //   BIT 11 WYNIKU
  //   S
  //   x1
  //   x2
  //   x3
  //   x4
  //   Cin
  //   Cout
  //   t1
  //   t2
  //   t3
  //   t4
  //   t6
  //   KOMPRESOR H
  //   t5
  //   Sum
  //   c_int
  //   Carry
  //   Cout
  //   A
  //   B
  //   S1
  //   C1
  //   cin
  //   BIT 12 WYNIKU
  //   Sum
  //   Cout
  //   x1
  //   x2
  //   x3
  //   x4
  //   Cin
  //   t1
  //   t2
  //   t3
  //   t4
  //   KOMPRESOR I
  //   t5
  //   t6
  //   BIT 13 WYNIKU
  //   Sum
  //   c_int
  //   Carry
  //   Cout
  //   A
  //   B
  //   S1
  //   C1
  //   cin
  //   BIT 14 WYNIKU
  //   Sum
  //   Cout
  //   BIT 15 WYNIKU
endmodule

module uklad_koncowy_4 (
  input  a0,
  input  a1,
  input  a2,
  input  a3,
  input  a4,
  input  a5,
  input  a6,
  input  a7,
  input  b0,
  input  b1,
  input  b2,
  input  b3,
  input  b4,
  input  b5,
  input  b6,
  input  b7,
  input  x4,
  output out_18,
  output out_19,
  output out_20,
  output out_21,
  output out_22,
  output out_23,
  output out_24,
  output out_25,
  output out_26,
  output out_27,
  output out_28,
  output out_29,
  output out_30,
  output out_31,
  output out_32,
  output out_33
);

  wire and_1_out, and_2_out, and_3_out, and_4_out, and_5_out, and_6_out, and_7_out, and_8_out, and_9_out,
       and_10_out, and_11_out, and_12_out, and_13_out, and_14_out, and_15_out, and_16_out, and_17_out,
       and_18_out, and_19_out, and_20_out, and_21_out, and_22_out, and_23_out, and_24_out, and_25_out,
       and_26_out, and_27_out, and_28_out, and_29_out, and_30_out, and_31_out, and_32_out, and_33_out,
       and_34_out, and_35_out, and_36_out, and_37_out, and_38_out, and_39_out, and_40_out, and_41_out,
       and_42_out, and_43_out, and_44_out, and_45_out, and_46_out, and_47_out, and_48_out, and_49_out,
       and_50_out, and_51_out, and_52_out, and_53_out, and_54_out, and_55_out, and_56_out, and_57_out,
       and_58_out, and_59_out, and_60_out, and_61_out, and_62_out, and_63_out, and_64_out, and_65_out,
       and_66_out, and_67_out, and_68_out, and_69_out, and_70_out, and_71_out, and_72_out, and_73_out,
       and_74_out, and_75_out, and_76_out, and_77_out, and_78_out, and_79_out, and_80_out, and_81_out,
       and_82_out, and_83_out, and_84_out, and_85_out, and_86_out, and_87_out, and_88_out, or_1_out,
       or_2_out, or_3_out, or_4_out, or_5_out, or_6_out, or_7_out, or_8_out, or_9_out, or_10_out, or_11_out,
       or_12_out, or_13_out, or_14_out, or_15_out, or_16_out, or_17_out, or_18_out, or_19_out, or_20_out,
       or_21_out, or_22_out, or_23_out, or_24_out, or_25_out, or_26_out, or_27_out, xor_1_out, xor_2_out,
       xor_3_out, xor_4_out, xor_5_out, xor_6_out, xor_7_out, xor_8_out, xor_9_out, xor_11_out, xor_12_out,
       xor_13_out, xor_14_out, xor_15_out, xor_16_out, xor_17_out, xor_18_out, xor_19_out, xor_20_out,
       xor_21_out, xor_22_out, xor_23_out, xor_24_out, xor_26_out, xor_27_out, xor_28_out, xor_29_out,
       xor_30_out, xor_31_out, xor_33_out, xor_34_out, xor_35_out, xor_36_out, xor_37_out, xor_38_out,
       xor_39_out, xor_41_out, xor_42_out, xor_43_out, xor_44_out, xor_45_out, xor_47_out, xor_48_out,
       xor_49_out, xor_51_out;

  and and_1 (and_1_out, b7, a0);
  and and_2 (and_2_out, b6, a1);
  and and_3 (and_3_out, b7, a1);
  and and_4 (and_4_out, b5, a2);
  and and_5 (and_5_out, b6, a2);
  and and_6 (and_6_out, b7, a2);
  and and_7 (and_7_out, b4, a3);
  and and_8 (and_8_out, b5, a3);
  and and_9 (and_9_out, b6, a3);
  and and_10 (and_10_out, b7, a3);
  and and_11 (and_11_out, b3, a4);
  and and_12 (and_12_out, b4, a4);
  and and_13 (and_13_out, b5, a4);
  and and_14 (and_14_out, b6, a4);
  and and_15 (and_15_out, b7, a4);
  and and_16 (and_16_out, b2, a5);
  and and_17 (and_17_out, b3, a5);
  and and_18 (and_18_out, b4, a5);
  and and_19 (and_19_out, b5, a5);
  and and_20 (and_20_out, b6, a5);
  and and_21 (and_21_out, b7, a5);
  and and_22 (and_22_out, b1, a6);
  and and_23 (and_23_out, b2, a6);
  and and_24 (and_24_out, b3, a6);
  and and_25 (and_25_out, b4, a6);
  and and_26 (and_26_out, b5, a6);
  and and_27 (and_27_out, b6, a6);
  and and_28 (and_28_out, b7, a6);
  and and_29 (and_29_out, b0, a7);
  and and_30 (and_30_out, b1, a7);
  and and_31 (and_31_out, b2, a7);
  and and_32 (and_32_out, b3, a7);
  and and_33 (and_33_out, b4, a7);
  and and_34 (and_34_out, b5, a7);
  and and_35 (and_35_out, b6, a7);
  and and_36 (and_36_out, b7, a7);
  or or_1 (or_1_out, and_1_out, and_2_out, and_4_out, and_7_out);
  or or_2 (or_2_out, and_11_out, and_16_out, and_22_out, and_29_out);
  xor xor_1 (xor_1_out, and_3_out, and_5_out);
  and and_37 (and_37_out, and_5_out, and_3_out);
  xor xor_2 (xor_2_out, and_17_out, and_23_out);
  and and_38 (and_38_out, and_23_out, and_17_out);
  xor xor_3 (xor_3_out, xor_1_out, and_8_out);
  and and_39 (and_39_out, and_8_out, xor_1_out);
  xor xor_4 (xor_4_out, xor_2_out, and_30_out);
  and and_40 (and_40_out, and_30_out, xor_2_out);
  xor xor_5 (xor_5_out, xor_3_out, and_12_out);
  and and_41 (and_41_out, and_12_out, xor_3_out);
  xor xor_6 (xor_6_out, xor_4_out, 1'b0);
  and and_42 (and_42_out, 1'b0, xor_4_out);
  xor xor_7 (xor_7_out, xor_5_out, 1'b0);
  and and_43 (and_43_out, 1'b0, xor_5_out);
  xor xor_8 (xor_8_out, xor_6_out, 1'b0);
  and and_44 (and_44_out, 1'b0, xor_6_out);
  or or_3 (or_3_out, and_39_out, and_41_out, and_43_out);
  or or_4 (or_4_out, and_39_out, and_37_out);
  or or_5 (or_5_out, and_40_out, and_42_out, and_44_out);
  or or_6 (or_6_out, and_40_out, and_38_out);
  xor xor_9 (xor_9_out, xor_7_out, xor_8_out);
  and and_45 (and_45_out, xor_7_out, xor_8_out);
  xor xor_10 (out_25, xor_9_out, or_1_out);
  and and_46 (and_46_out, xor_9_out, or_1_out);
  or or_7 (or_7_out, and_46_out, and_45_out);
  xor xor_11 (xor_11_out, and_6_out, and_9_out);
  and and_47 (and_47_out, and_9_out, and_6_out);
  xor xor_12 (xor_12_out, and_24_out, and_31_out);
  and and_48 (and_48_out, and_31_out, and_24_out);
  xor xor_13 (xor_13_out, xor_11_out, and_13_out);
  and and_49 (and_49_out, and_13_out, xor_11_out);
  xor xor_14 (xor_14_out, xor_12_out, or_4_out);
  and and_50 (and_50_out, or_4_out, xor_12_out);
  xor xor_15 (xor_15_out, xor_13_out, and_18_out);
  and and_51 (and_51_out, and_18_out, xor_13_out);
  xor xor_16 (xor_16_out, xor_14_out, or_5_out);
  and and_52 (and_52_out, or_5_out, xor_14_out);
  xor xor_17 (xor_17_out, xor_15_out, or_3_out);
  and and_53 (and_53_out, or_3_out, xor_15_out);
  xor xor_18 (xor_18_out, xor_16_out, or_6_out);
  and and_54 (and_54_out, or_6_out, xor_16_out);
  or or_8 (or_8_out, and_49_out, and_51_out, and_53_out);
  or or_9 (or_9_out, and_49_out, and_47_out);
  or or_10 (or_10_out, and_50_out, and_52_out, and_54_out);
  or or_11 (or_11_out, and_50_out, and_48_out);
  xor xor_19 (xor_19_out, xor_17_out, xor_18_out);
  and and_55 (and_55_out, xor_18_out, xor_17_out);
  xor xor_20 (xor_20_out, xor_19_out, or_7_out);
  and and_56 (and_56_out, or_7_out, xor_19_out);
  xor xor_21 (xor_21_out, and_10_out, and_14_out);
  and and_57 (and_57_out, and_14_out, and_10_out);
  xor xor_22 (xor_22_out, xor_20_out, x4);
  and and_58 (and_58_out, x4, xor_20_out);
  xor xor_23 (xor_23_out, and_32_out, or_9_out);
  and and_59 (and_59_out, or_9_out, and_32_out);
  xor xor_24 (xor_24_out, xor_21_out, and_19_out);
  and and_60 (and_60_out, and_19_out, xor_21_out);
  xor xor_25 (out_24, xor_22_out, or_2_out);
  and and_61 (and_61_out, or_2_out, xor_22_out);
  xor xor_26 (xor_26_out, xor_23_out, or_10_out);
  and and_62 (and_62_out, or_10_out, xor_23_out);
  xor xor_27 (xor_27_out, xor_24_out, and_25_out);
  and and_63 (and_63_out, and_25_out, xor_24_out);
  or or_12 (or_12_out, and_56_out, and_58_out, and_61_out);
  or or_13 (or_13_out, and_56_out, and_55_out);
  xor xor_28 (xor_28_out, xor_26_out, or_11_out);
  and and_64 (and_64_out, or_11_out, xor_26_out);
  xor xor_29 (xor_29_out, xor_27_out, or_8_out);
  and and_65 (and_65_out, or_8_out, xor_27_out);
  xor xor_30 (xor_30_out, xor_28_out, or_12_out);
  and and_66 (and_66_out, or_12_out, xor_28_out);
  or or_14 (or_14_out, and_60_out, and_63_out, and_65_out);
  or or_15 (or_15_out, and_60_out, and_57_out);
  or or_16 (or_16_out, and_62_out, and_64_out, and_66_out);
  or or_17 (or_17_out, and_62_out, and_59_out);
  xor xor_31 (xor_31_out, xor_29_out, xor_30_out);
  and and_67 (and_67_out, xor_29_out, xor_30_out);
  xor xor_32 (out_23, xor_31_out, or_13_out);
  and and_68 (and_68_out, xor_31_out, or_13_out);
  xor xor_33 (xor_33_out, and_15_out, and_20_out);
  and and_69 (and_69_out, and_20_out, and_15_out);
  or or_18 (or_18_out, and_68_out, and_67_out);
  xor xor_34 (xor_34_out, xor_33_out, and_26_out);
  and and_70 (and_70_out, and_26_out, xor_33_out);
  xor xor_35 (xor_35_out, or_15_out, or_16_out);
  and and_71 (and_71_out, or_15_out, or_16_out);
  xor xor_36 (xor_36_out, xor_34_out, and_33_out);
  and and_72 (and_72_out, and_33_out, xor_34_out);
  and and_73 (and_73_out, xor_35_out, or_17_out);
  xor xor_37 (xor_37_out, xor_36_out, or_14_out);
  and and_74 (and_74_out, or_14_out, xor_36_out);
  xor xor_38 (xor_38_out, xor_35_out, or_17_out);
  or or_19 (or_19_out, and_73_out, and_71_out);
  or or_20 (or_20_out, and_70_out, and_72_out, and_74_out);
  or or_21 (or_21_out, and_70_out, and_69_out);
  xor xor_39 (xor_39_out, xor_37_out, xor_38_out);
  and and_75 (and_75_out, xor_37_out, xor_38_out);
  xor xor_40 (out_22, xor_39_out, or_18_out);
  and and_76 (and_76_out, xor_39_out, or_18_out);
  or or_22 (or_22_out, and_76_out, and_75_out);
  xor xor_41 (xor_41_out, and_21_out, and_27_out);
  and and_77 (and_77_out, and_27_out, and_21_out);
  xor xor_42 (xor_42_out, xor_41_out, and_34_out);
  and and_78 (and_78_out, and_34_out, xor_41_out);
  xor xor_43 (xor_43_out, xor_42_out, or_20_out);
  and and_79 (and_79_out, or_20_out, xor_42_out);
  xor xor_44 (xor_44_out, xor_43_out, or_21_out);
  and and_80 (and_80_out, or_21_out, xor_43_out);
  or or_23 (or_23_out, and_78_out, and_79_out, and_80_out);
  or or_24 (or_24_out, and_78_out, and_77_out);
  xor xor_45 (xor_45_out, xor_44_out, or_19_out);
  and and_81 (and_81_out, xor_44_out, or_19_out);
  xor xor_46 (out_21, xor_45_out, or_22_out);
  and and_82 (and_82_out, xor_45_out, or_22_out);
  or or_25 (or_25_out, and_82_out, and_81_out);
  xor xor_47 (xor_47_out, and_28_out, and_35_out);
  and and_83 (and_83_out, and_35_out, and_28_out);
  and and_84 (and_84_out, or_23_out, xor_47_out);
  xor xor_48 (xor_48_out, xor_47_out, or_23_out);
  xor xor_49 (xor_49_out, xor_48_out, or_24_out);
  and and_85 (and_85_out, or_24_out, xor_48_out);
  and and_86 (and_86_out, or_25_out, xor_49_out);
  xor xor_50 (out_20, xor_49_out, or_25_out);
  or or_26 (or_26_out, and_84_out, and_85_out, and_86_out);
  or or_27 (or_27_out, and_84_out, and_83_out);
  xor xor_51 (xor_51_out, and_36_out, or_26_out);
  and and_87 (and_87_out, and_36_out, or_26_out);
  xor xor_52 (out_19, xor_51_out, or_27_out);
  and and_88 (and_88_out, xor_51_out, or_27_out);
  or or_28 (out_18, and_88_out, and_87_out);

  assign out_26 = 1'b0;
  assign out_27 = 1'b0;
  assign out_28 = 1'b0;
  assign out_29 = 1'b0;
  assign out_30 = 1'b0;
  assign out_31 = 1'b1;
  assign out_32 = 1'b1;
  assign out_33 = 1'b0;

  // Notes on the sheet:
  //   a0
  //   a1
  //   a2
  //   a3
  //   a4
  //   a5
  //   a6
  //   a7
  //   4
  //   9
  //   11
  //   12
  //   13
  //   14
  //   8
  //   10
  //   Carry_8
  //   Carry_9
  //   x1
  //   x2
  //   x3
  //   x4
  //   Cin
  //   x1
  //   x2
  //   x3
  //   x4
  //   Cin
  //   t1
  //   t2
  //   t1
  //   t2
  //   t3
  //   t4
  //   t4
  //   KOMPRESOR B
  //   KOMPRESOR A
  //   t3
  //   t5
  //   t6
  //   t5
  //   t6
  //   Sum
  //   c_int
  //   Sum
  //   c_int
  //   Carry
  //   Cout
  //   Carry
  //   Cout
  //   B
  //   A
  //   S1
  //   C1
  //   tutaj cin to bedzie z pierwszego ora z ecm
  //   cin
  //   S
  //   bit 8 wyniku
  //   Cout
  //   do kolumny 9
  //   x1
  //   x2
  //   x3
  //   x4
  //   CIN (carry komp a)
  //   Cin
  //   x1
  //   x2
  //   x3
  //   x4
  //   t1
  //   t2
  //   t1
  //   t2
  //   t3
  //   t4
  //   t4
  //   t3
  //   KOMPRESOR D
  //   KOMPRESOR C
  //   t5
  //   t6
  //   t5
  //   t6
  //   Sum
  //   c_int
  //   Sum
  //   c_int
  //   Carry
  //   Cout
  //   Carry
  //   Cout
  //   x1
  //   x2
  //   x3
  //   Cin
  //   tu cin bedzie z 2 ora z ecm
  //   t1
  //   t2
  //   x1
  //   x2
  //   x3
  //   x4
  //   Cin
  //   x1
  //   x2
  //   x3
  //   x4
  //   Cin
  //   t3
  //   t4
  //   t1
  //   t2
  //   t5
  //   t6
  //   t1
  //   t2
  //   TUTAJ KOMPRESOR ZAMIAST SUMATORA WYJATKOWO
  //   BIT 9 WYNIKOWY
  //   t3
  //   t4
  //   Sum
  //   c_int
  //   t3
  //   t4
  //   KOMPRESOR E
  //   KOMPRESOR F
  //   Carry
  //   Cout
  //   t5
  //   t6
  //   t5
  //   t6
  //   Sum
  //   c_int
  //   Sum
  //   c_int
  //   Carry
  //   Cout
  //   Carry
  //   Cout
  //   A
  //   B
  //   x1
  //   x2
  //   x3
  //   x4
  //   Cin
  //   cin
  //   S1
  //   C1
  //   t1
  //   BIT WYNIKOWY 10 KOLUMNY
  //   S
  //   t2
  //   Cout
  //   t4
  //   A
  //   B
  //   t3
  //   S1
  //   C1
  //   KOMPRESOR G
  //   t5
  //   t6
  //   cin
  //   Sum
  //   c_int
  //   S
  //   Cout
  //   Carry
  //   Cout
  //   A
  //   B
  //   S1
  //   C1
  //   cin
  //   BIT 11 WYNIKU
  //   S
  //   x1
  //   x2
  //   x3
  //   x4
  //   Cin
  //   Cout
  //   t1
  //   t2
  //   t3
  //   t4
  //   t6
  //   KOMPRESOR H
  //   t5
  //   Sum
  //   c_int
  //   Carry
  //   Cout
  //   A
  //   B
  //   S1
  //   C1
  //   cin
  //   BIT 12 WYNIKU
  //   Sum
  //   Cout
  //   x1
  //   x2
  //   x3
  //   x4
  //   Cin
  //   t1
  //   t2
  //   t3
  //   t4
  //   KOMPRESOR I
  //   t5
  //   t6
  //   BIT 13 WYNIKU
  //   Sum
  //   c_int
  //   Carry
  //   Cout
  //   A
  //   B
  //   S1
  //   C1
  //   cin
  //   BIT 14 WYNIKU
  //   Sum
  //   Cout
  //   BIT 15 WYNIKU
endmodule
